// Logisim project BCD_c.circ as structural Verilog: 1 circuit, main circuit BCD_c2
module BCD_c2 (
  input  A,
  input  B,
  input  C,
  input  D,
  output c_2
);

  wire nand_1_out, nand_2_out, nand_3_out, not_1_out, not_2_out, not_3_out;

  not not_1 (not_1_out, A);
  not not_2 (not_2_out, B);
  not not_3 (not_3_out, D);
  nand nand_1 (nand_1_out, not_1_out, not_2_out, C, not_3_out);
  nand nand_2 (nand_2_out, A, B, not_3_out);
  nand nand_3 (nand_3_out, A, B, C);
  nand nand_4 (c_2, nand_1_out, nand_2_out, nand_3_out);
endmodule
